# Fritzing sketch circuit_fzz (saved by Fritzing 0.9.4)
breadboards: 1

parts:
  Part3 = Arduino Uno (Rev3)
  LED6 = LED - 5mm [color="White (6500K)" package="5 mm [THT]"]
  R4 = Resistor [tolerance=±5% resistance=330 package=THT]
  R5 = Resistor [tolerance=±5% resistance=10 package=THT]
  S1 = Pushbutton [package="[SMD]"]

nets:
  N1: Part3.D2, R4.Pin_0
  N2: Part3.D3_PWM, R5.Pin_1, S1.Pin_3, S1.Pin_4
  N3: Part3.5V, S1.Pin_1, S1.Pin_2
  N4: Part3.GND, LED6.cathode, R5.Pin_0
  N5: LED6.anode, R4.Pin_1
