# Fritzing sketch circuit_fzz (saved by Fritzing 0.9.3b)
breadboards: 1

parts:
  Part3 = Arduino Uno (Rev3)
  LED4 = LED - 5mm [color="Red (633nm)" package="5 mm [THT]"]
  LED5 = LED - 5mm [color="Yellow (585nm)" package="5 mm [THT]"]
  LED6 = LED - 5mm [color="Green (560nm)" package="5 mm [THT]"]
  R4 = Resistor [tolerance=±5% resistance=330 package=THT]
  R5 = Resistor [tolerance=±5% resistance=330 package=THT]
  R6 = Resistor [tolerance=±5% resistance=330 package=THT]

nets:
  N1: Part3.D2, R4.Pin_0
  N2: Part3.D3_PWM, R5.Pin_0
  N3: Part3.D4, R6.Pin_0
  N4: Part3.GND, LED4.cathode, LED5.cathode, LED6.cathode
  N5: LED4.anode, R6.Pin_1
  N6: LED5.anode, R5.Pin_1
  N7: LED6.anode, R4.Pin_1
