# Fritzing sketch circuit_fzz (saved by Fritzing 0.9.3b)
breadboards: 1

parts:
  Part3 = Arduino Uno (Rev3)
  LED5 = LED - 5mm [color="White (6500K)" package="5 mm [THT]"]
  R5 = Resistor [tolerance=±5% resistance=330 package=THT]
  R6 = Photocell (LDR) [package=THT]
  R7 = Resistor [tolerance=±5% resistance=330 package=THT]

nets:
  N1: Part3.A0, R6.pin_0, R7.Pin_1
  N2: Part3.D3_PWM, R5.Pin_0
  N3: Part3.5V, R6.pin_1
  N4: Part3.GND, LED5.cathode, R7.Pin_0
  N5: LED5.anode, R5.Pin_1
