# Fritzing sketch circuit_fzz (saved by Fritzing 0.9.3b)
breadboards: 1

parts:
  Part3 = Arduino Uno (Rev3)
  LED5 = LED - 5mm [color="Red (635nm)" package="5 mm [THT]"]
  R5 = Resistor [tolerance=±5% resistance=330 package=THT]
  J1 = Piezo Speaker

nets:
  N1: Part3.D3_PWM, R5.Pin_0
  N2: Part3.D4, J1.pin2
  N3: Part3.GND, LED5.cathode, J1.pin1
  N4: LED5.anode, R5.Pin_1
