# Fritzing sketch circuit_fzz (saved by Fritzing 0.9.3b)
breadboards: 1

parts:
  Part1 = Arduino Uno (Rev3)
  LED1 = LED - 5mm [color="Green (560nm)" package="5 mm [THT]"]
  LED2 = LED - 5mm [color="Yellow (585nm)" package="5 mm [THT]"]
  LED3 = LED - 5mm [color="Red (633nm)" package="5 mm [THT]"]
  R1 = Resistor [tolerance=±5% resistance=330 package=THT]
  R2 = Resistor [tolerance=±5% resistance=330 package=THT]
  R3 = Resistor [tolerance=±5% resistance=330 package=THT]
  Part2 = Soil Moisture Sensor
  J1 = Piezo Speaker

nets:
  N1: Part1.A0, Part2.SIG
  GND: Part1.GND, LED1.cathode, LED2.cathode, LED3.cathode, Part2.GND, J1.pin1
  N2: Part1.D2, R1.Pin_0
  N3: Part1.D3_PWM, R2.Pin_0
  N4: Part1.D4, R3.Pin_0
  N5: Part1.D5_PWM, J1.pin2
  5V: Part1.5V, Part2.VCC
  N6: LED1.anode, R1.Pin_1
  N7: LED2.anode, R2.Pin_1
  N8: LED3.anode, R3.Pin_1
