# Fritzing sketch circuit_fzz (saved by Fritzing 0.9.3b)
breadboards: 1

parts:
  Part1 = Arduino Uno (Rev3)
  J1 = Piezo Speaker
  S1 = Pushbutton [package="[THT]"]
  R14 = Resistor [tolerance=±5% resistance=10k package=THT]
  S2 = Pushbutton [package="[THT]"]
  S3 = Pushbutton [package="[THT]"]
  S4 = Pushbutton [package="[THT]"]
  R15 = Resistor [tolerance=±5% resistance=10k package=THT]
  R16 = Resistor [tolerance=±5% resistance=10k package=THT]
  R17 = Resistor [tolerance=±5% resistance=10k package=THT]
  LED1 = LED - 5mm [color="Yellow (592nm)" package="5 mm [THT]"]
  LED2 = LED - 5mm [color="Green (565nm)" package="5 mm [THT]"]
  LED3 = LED - 5mm [color="Red (633nm)" package="5 mm [THT]"]
  R18 = Resistor [tolerance=±5% resistance=330 package=THT]
  R19 = Resistor [tolerance=±5% resistance=330 package=THT]
  R20 = Resistor [tolerance=±5% resistance=330 package=THT]

nets:
  N1: Part1.D8, R19.Pin_0
  N2: Part1.D9_PWM, R18.Pin_0
  N3: Part1.GND, J1.pin1, R14.Pin_0, R15.Pin_0, R16.Pin_0, R17.Pin_0, LED1.cathode, LED2.cathode, LED3.cathode
  N4: Part1.D2, S4.Pin_3, S4.Pin_4, R17.Pin_1
  N5: Part1.D3_PWM, S3.Pin_3, S3.Pin_4, R16.Pin_1
  N6: Part1.D4, S2.Pin_3, S2.Pin_4, R15.Pin_1
  N7: Part1.D5_PWM, S1.Pin_3, S1.Pin_4, R14.Pin_1
  N8: Part1.D6_PWM, J1.pin2
  N9: Part1.D7, R20.Pin_0
  N10: Part1.5V, S1.Pin_1, S1.Pin_2, S2.Pin_1, S2.Pin_2, S3.Pin_1, S3.Pin_2, S4.Pin_1, S4.Pin_2
  N11: LED1.anode, R20.Pin_1
  N12: LED2.anode, R19.Pin_1
  N13: LED3.anode, R18.Pin_1
