# Fritzing sketch circuit_fzz (saved by Fritzing 0.9.3b)
breadboards: 1

parts:
  Part1 = Arduino Uno (Rev3)
  LED1 = LED - 5mm [color="White (6500K)" package="5 mm [THT]"]
  LED2 = LED - 5mm [color="White (6500K)" package="5 mm [THT]"]
  LED3 = LED - 5mm [color="White (6500K)" package="5 mm [THT]"]
  R1 = Resistor [tolerance=±5% resistance=330 package=THT]
  J1 = Piezo Speaker
  LED4 = LED - 5mm [color="White (6500K)" package="5 mm [THT]"]
  LED5 = LED - 5mm [color="White (6500K)" package="5 mm [THT]"]
  LED6 = LED - 5mm [color="Red (635nm)" package="5 mm [THT]"]
  LED7 = LED - 5mm [color="White (6500K)" package="5 mm [THT]"]
  LED8 = LED - 5mm [color="White (6500K)" package="5 mm [THT]"]
  LED9 = LED - 5mm [color="White (6500K)" package="5 mm [THT]"]
  LED10 = LED - 5mm [color="White (6500K)" package="5 mm [THT]"]
  LED11 = LED - 5mm [color="White (6500K)" package="5 mm [THT]"]
  R4 = Resistor [tolerance=±5% resistance=330 package=THT]
  R5 = Resistor [tolerance=±5% resistance=330 package=THT]
  R6 = Resistor [tolerance=±5% resistance=330 package=THT]
  R7 = Resistor [tolerance=±5% resistance=330 package=THT]
  R8 = Resistor [tolerance=±5% resistance=330 package=THT]
  R9 = Resistor [tolerance=±5% resistance=330 package=THT]
  R10 = Resistor [tolerance=±5% resistance=330 package=THT]
  R11 = Resistor [tolerance=±5% resistance=330 package=THT]
  R12 = Resistor [tolerance=±5% resistance=330 package=THT]
  R13 = Resistor [tolerance=±5% resistance=330 package=THT]
  S1 = Pushbutton [package="[THT]"]
  R14 = Resistor [tolerance=±5% resistance=10k package=THT]

nets:
  N1: Part1.A0, S1.Pin_3, S1.Pin_4, R14.Pin_1
  N2: Part1.D8, R7.Pin_1
  N3: Part1.D9_PWM, R6.Pin_1
  N4: Part1.D10_PWM/SS, R5.Pin_1
  N5: Part1.D11_PWM/MOSI, R12.Pin_1
  N6: Part1.D12/MISO, R13.Pin_1
  N7: Part1.D13/SCK, J1.pin2
  N8: Part1.D2, R1.Pin_1
  N9: Part1.D3_PWM, R4.Pin_1
  N10: Part1.D4, R11.Pin_1
  N11: Part1.D5_PWM, R10.Pin_1
  N12: Part1.D6_PWM, R9.Pin_1
  N13: Part1.D7, R8.Pin_1
  N14: Part1.GND, LED1.cathode, LED2.cathode, LED3.cathode, J1.pin1, LED4.cathode, LED5.cathode, LED6.cathode, LED7.cathode, LED8.cathode, LED9.cathode, LED10.cathode, LED11.cathode, S1.Pin_1, S1.Pin_2, R14.Pin_0
  N15: LED1.anode, R1.Pin_0
  N16: LED2.anode, R4.Pin_0
  N17: LED3.anode, R11.Pin_0
  N18: LED4.anode, R10.Pin_0
  N19: LED5.anode, R9.Pin_0
  N20: LED6.anode, R8.Pin_0
  N21: LED7.anode, R7.Pin_0
  N22: LED8.anode, R6.Pin_0
  N23: LED9.anode, R5.Pin_0
  N24: LED10.anode, R12.Pin_0
  N25: LED11.anode, R13.Pin_0
